# Fritzing sketch Waterelf32-protoboard (saved by Fritzing 0.9.3b)

parts:
  Part2 = Adafruit FeatherWing Proto [part_number="Adafruit #2884"]
  J1 = male pin header, 4 pins [form="♂ (male)"]
  J2 = male pin header, 4 pins [form="♂ (male)"]
  J3 = male pin header, 3 pins [form="♂ (male)"]
  J4 = male pin header, 3 pins [form="♂ (male)"]
  J8 = male pin header, 3 pins [form="♂ (male)"]
  J9 = male pin header, 3 pins [form="♂ (male)"]
  J10 = male pin header, 3 pins [form="♂ (male)"]
  J6 = male pin header, 6 pins [form="♂ (male)"]
  J5 = male pin header, 6 pins [form="♂ (male)"]
  J7 = male pin header, 6 pins [form="♂ (male)"]
  U1 = FS1000A - 433Mhz RF Transmitter [package=THT]  # not connected

nets:
  N1: Part2.3V, J3.pin2, J4.pin2
  N2: Part2.GND, J3.pin3, J4.pin3, J6.pin1, J5.pin1, J7.pin1
  N3: Part2.N$50, J3.pin1
  N4: Part2.N$52, J4.pin1
  N5: Part2.N$64, J6.pin2
  N6: Part2.N$65, J6.pin3
  N7: Part2.N$66, J6.pin4
  N8: Part2.N$68, J5.pin2
  N9: Part2.N$70, J7.pin2
  N10: Part2.N$71, J7.pin3
  N11: Part2.N$73, J5.pin3
  N12: Part2.N$76, J5.pin4
  N13: Part2.N$78, J7.pin4
  N14: Part2.N$79, J7.pin5
  N15: Part2.N$81, J6.pin5
  N16: Part2.N$83, J5.pin5
  N17: Part2.N$84, J7.pin6
  N18: Part2.N$86, J5.pin6
  N19: Part2.N$88, J6.pin6
  N20: Part2.N$94, J10.pin1
  N21: Part2.N$96, J9.pin1
  N22: Part2.N$98, J8.pin1
  N23: Part2.N$99, J8.pin2
  N24: Part2.N$101, J9.pin2
  N25: Part2.N$103, J10.pin2
  N26: Part2.N$104, J10.pin3
  N27: Part2.N$106, J9.pin3
  N28: Part2.N$108, J8.pin3
  N29: Part2.N$116, J1.pin1
  N30: Part2.N$118, J2.pin1
  N31: Part2.N$120, J2.pin2
  N32: Part2.N$122, J1.pin2
  N33: Part2.N$126, J1.pin4
  N34: Part2.N$128, J2.pin4
  N35: Part2.N$131, J2.pin3
  N36: Part2.N$133, J1.pin3

custom parts:
  Adafruit FeatherWing Proto: This is the FeatherWing Proto - a prototyping add-on for all Feather boards. Using our Feather Stacking Headers or Feather Female Headers you can connect a FeatherWing on top or bottom of your Feather board and let the board take flight! This has a duplicate breakout for each pin on a Feather, as well as a bunch of plain grid proto holes. For GND and 3.3V, we give you a strip of connected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
  FS1000A - 433Mhz RF Transmitter: This is 433Mhz RF transmitter with receiver kit for Arduino ARM MCU wireless Application environment: Remote control switch, receiver module, motorcycles, automobile anti-theft products, home security products, electric doors, shutter doors, windows, remote control socket, remote control LED, remote audio remote control electric doors, garage door remote control, remote control retractable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
